# Fritzing sketch Untitled Sketch (saved by Fritzing 0.9.2b)
breadboards: 1

parts:
  부품1 = Arduino Leonardo (Rev3b)
  부품2 = Arduino Mega ADK (Rev3)
  J1 = Basic Servo
  J22 = Basic Servo
  J23 = Basic Servo
  J24 = Basic Servo
  J25 = Basic Servo
  J26 = Basic Servo
  J27 = Basic Servo
  J28 = Basic Servo
  J29 = Basic Servo
  J30 = Basic Servo
  J31 = Basic Servo
  J33 = Basic Servo
  J34 = Basic Servo
  J35 = Basic Servo
  J36 = Basic Servo
  J37 = Basic Servo
  J38 = Basic Servo
  J39 = Basic Servo
  J40 = Basic Servo
  J41 = Basic Servo
  S1 = Pushbutton [package="[THT]"]
  R1 = Resistor [tolerance=±5% resistance=220 package=THT]

nets:
  N1: 부품1.D3_PWM/SCL, J26.pulse
  N2: 부품1.D5_PWM, J27.pulse
  N3: 부품1.D6_PWM/A7, J28.pulse
  N4: 부품1.5V, S1.Pin_1, S1.Pin_2, R1.Pin_1
  N5: 부품1.GND, R1.Pin_0
  N6: 부품1.D8/A8, S1.Pin_3, S1.Pin_4
  N7: 부품1.D9_PWM/A9, J29.pulse
  N8: 부품1.D10_PWM/A10, J30.pulse
  N9: 부품2.D13_PWM, J25.pulse
  N10: 부품2.D12_PWM, J24.pulse
  N11: 부품2.D11_PWM, J23.pulse
  N12: 부품2.D10_PWM, J22.pulse
  N13: 부품2.D9_PWM, J1.pulse
  N14: 부품2.D2_PWM, J38.pulse
  N15: 부품2.D3_PWM, J37.pulse
  N16: 부품2.D4_PWM, J36.pulse
  N17: 부품2.D5_PWM, J35.pulse
  N18: 부품2.D6_PWM, J34.pulse
  N19: 부품2.D44, J41.pulse
  N20: 부품2.D45, J40.pulse
  N21: 부품2.D46, J39.pulse
  GND: J1.gnd, J22.gnd, J23.gnd, J24.gnd, J25.gnd, J26.gnd, J27.gnd, J28.gnd, J29.gnd, J30.gnd, J33.gnd, J34.gnd, J35.gnd, J36.gnd, J37.gnd, J38.gnd, J39.gnd, J40.gnd, J41.gnd
  VCC: J1.vcc, J22.vcc, J23.vcc, J24.vcc, J25.vcc, J26.vcc, J27.vcc, J28.vcc, J29.vcc, J30.vcc, J31.vcc, J33.vcc, J34.vcc, J35.vcc, J36.vcc, J37.vcc, J38.vcc, J39.vcc, J40.vcc, J41.vcc
